# Fritzing sketch 16-pixel-display (saved by Fritzing 0.9.3b)
breadboards: 1

parts:
  IC1 = MCP23017 I2C I/O Expander
  Raspberry_Pi_1 = Raspberry Pi 3 [part_number=RPI-3-V1.2]
  R1 = Resistor [tolerance=±5% resistance=330 package="0402 [SMD]"]
  R2 = Resistor [tolerance=±5% resistance=330 package="0805 [SMD]"]
  R3 = Resistor [tolerance=±5% resistance=330 package="0402 [SMD]"]
  R4 = Resistor [tolerance=±5% resistance=330 package="0402 [SMD]"]
  LED1 = LED - 5mm [color="Red (633nm)" package="5 mm [THT]"]  # not connected
  LED2 = LED - 5mm [color="Red (633nm)" package="5 mm [THT]"]
  LED3 = LED - 5mm [color="Red (633nm)" package="5 mm [THT]"]  # not connected
  LED4 = LED - 5mm [color="Red (633nm)" package="5 mm [THT]"]  # not connected
  LED5 = LED - 5mm [color="Red (633nm)" package="5 mm [THT]"]  # not connected
  LED6 = LED - 5mm [color="Red (633nm)" package="5 mm [THT]"]  # not connected
  LED7 = LED - 5mm [color="Red (633nm)" package="5 mm [THT]"]  # not connected
  LED8 = LED - 5mm [color="Red (633nm)" package="5 mm [THT]"]
  LED9 = LED - 5mm [color="Red (633nm)" package="5 mm [THT]"]  # not connected
  LED10 = LED - 5mm [color="Red (633nm)" package="5 mm [THT]"]  # not connected
  LED11 = LED - 5mm [color="Red (633nm)" package="5 mm [THT]"]  # not connected
  LED12 = LED - 5mm [color="Red (633nm)" package="5 mm [THT]"]
  LED13 = LED - 5mm [color="Red (633nm)" package="5 mm [THT]"]
  LED14 = LED - 5mm [color="Red (633nm)" package="5 mm [THT]"]
  LED15 = LED - 5mm [color="Red (633nm)" package="5 mm [THT]"]
  LED16 = LED - 5mm [color="Red (633nm)" package="5 mm [THT]"]

nets:
  N1: IC1.A0, IC1.A1, IC1.A2, IC1.RESET, Raspberry_Pi_1.GND
  N2: IC1.GPA0, LED13.anode
  N3: IC1.GPA1, LED14.anode
  N4: IC1.GPA2, LED15.anode
  N5: IC1.GPA3, LED16.anode
  N6: IC1.GPA4, R4.Pin_0
  N7: IC1.GPA5, R1.Pin_0
  N8: IC1.GPA6, R2.Pin_0
  N9: IC1.GPA7, R3.Pin_0
  N10: R1.Pin_1, LED8.cathode
  N11: R2.Pin_1, LED12.cathode
  N12: R3.Pin_1, LED16.cathode
  N13: R4.Pin_1, LED2.cathode

notes:
  Cathodes
  Anodes

custom parts:
  MCP23017 I2C I/O Expander: The MCP23017 uses two i2c pins (these can be shared with other i2c devices), and in exchange gives you 16 general purpose pins. You can set each of 16 pins to be input, output, input with a pullup or open drain. There's even the ability to get an interrupt via an external pin when any of the inputs change so you don't have to keep polling the chip.
